// Logisim project schematic.circ as structural Verilog: 2 circuits, main circuit main
module main (
  input  [3:0] a,
  input  sub_notadd,
  input  [3:0] b,
  output [3:0] s,
  output cout
);

  wire adder0_cout, adder1_cout, adder2_cout, xor_1_out, xor_2_out, xor_3_out, xor_4_out;

  xor xor_1 (xor_1_out, sub_notadd, b[0]);
  xor xor_2 (xor_2_out, sub_notadd, b[1]);
  xor xor_3 (xor_3_out, sub_notadd, b[2]);
  xor xor_4 (xor_4_out, sub_notadd, b[3]);
  full_adder adder0 (.a(a[0]), .b(xor_1_out), .cin(sub_notadd), .S(s[0]), .cout(adder0_cout));
  full_adder adder1 (.a(a[1]), .b(xor_2_out), .cin(adder0_cout), .S(s[1]), .cout(adder1_cout));
  full_adder adder2 (.a(a[2]), .b(xor_3_out), .cin(adder1_cout), .S(s[2]), .cout(adder2_cout));
  full_adder adder3 (.a(a[3]), .b(xor_4_out), .cin(adder2_cout), .S(s[3]), .cout(cout));
endmodule

module full_adder (
  input  a,
  input  b,
  input  cin,
  output S,
  output cout
);

  wire and_1_out, and_2_out, xor_1_out;

  xor xor_1 (xor_1_out, a, b);
  and and_1 (and_1_out, a, b);
  xor xor_2 (S, xor_1_out, cin);
  and and_2 (and_2_out, xor_1_out, cin);
  or or_1 (cout, and_1_out, and_2_out);
endmodule
