// Logisim project schematic.circ as structural Verilog: 1 circuit, main circuit main
module main (
  input  [31:0] dividend,
  input  start,
  input  [31:0] divisor,
  input  clk,
  output done,
  output [31:0] quotient,
  output [31:0] remainder
);

  wire comparator_1_lt, hi;
  wire [0:0] q_reg_q_2;
  wire [30:0] multiplexer_3_out;
  wire [31:0] a_reg_q, multiplexer_2_out, subtractor_1_out;
  wire [31:1] q_reg_q;
  wire [31:31] multiplexer_3_out_2;
  wire [63:0] counter_q, multiplexer_1_out, subtractor_2_out;

  Register #(.width(64)) counter (.D(multiplexer_1_out), .en(1'b1), .clk(clk), .Q(counter_q), .clr(1'b0));
  Multiplexer #(.width(64)) multiplexer_1 (.in0(subtractor_2_out), .in1(64'h20), .out(multiplexer_1_out), .sel(start));
  Multiplexer #(.width(32)) multiplexer_2 (.in0({q_reg_q, hi}), .in1(dividend), .out(multiplexer_2_out), .sel(start));
  Register #(.width(32)) q_reg (.D(multiplexer_2_out), .en(1'b1), .clk(clk), .Q({q_reg_q_2[0], q_reg_q}), .clr(1'b0));
  Register #(.width(32)) a_reg (.D({multiplexer_3_out, q_reg_q_2[0]}), .en(1'b1), .clk(clk), .Q(a_reg_q), .clr(start));
  Subtractor #(.width(32)) subtractor_1 (.a(a_reg_q), .b(divisor), .out(subtractor_1_out), .bin(1'b0));  // open: bout
  Comparator #(.width(32)) comparator_1 (.a(a_reg_q), .b(divisor), .lt(comparator_1_lt));  // open: gt, eq
  Comparator #(.width(64)) comparator_2 (.a(counter_q), .b({64{1'b0}}), .eq(done));  // open: gt, lt
  Subtractor #(.width(64)) subtractor_2 (.a(counter_q), .b(64'h1), .out(subtractor_2_out), .bin(1'b0));  // open: bout
  Multiplexer #(.width(32)) multiplexer_3 (
    .in0(a_reg_q), .in1(subtractor_1_out), .out({multiplexer_3_out_2[31], multiplexer_3_out}), .sel(hi));
  not not_1 (hi, comparator_1_lt);
  Register #(.width(32)) register_1 (.D({q_reg_q, hi}), .en(done), .clk(clk), .Q(quotient));  // open: clr
  Register #(.width(32)) register_2 (
    .D({multiplexer_3_out_2[31], multiplexer_3_out}), .en(done), .clk(clk), .Q(remainder));  // open: clr
endmodule
