// Logisim project schematic.circ as structural Verilog: 12 circuits, main circuit main
module main (
  input  [31:0] a,
  input  [31:0] b,
  input  output_inc,
  input  [3:0] aluop,
  input  output_inverted,
  input  clk,
  input  rst,
  output [31:0] res_low,
  output [31:0] res_high,
  output done
);

  wire csa_2_cout;
  wire [31:0] Annd, not_1_out, not_2_out, oor, xoor;
  wire [32:0] ADD;
  wire [63:0] adder_1_out, CLOO, CLZ, diiv, MUL, multiplexer_1_out, multiplexer_3_out, not_3_out, ROTR,
       SLL11, SRA1, SRL1, SUB;

  assign not_1_out = ~b;  // NOT_Gate not_1, 32 bits wide
  assign not_2_out = ~a;  // NOT_Gate not_2, 32 bits wide
  CSA csa_1 (.cin(1'b0), .A(a), .B(b), .SUM(ADD[31:0]), .cout(ADD[32]));
  CSA csa_2 (.cin(1'b1), .A(a), .B(not_1_out), .SUM(SUB[31:0]), .cout(csa_2_cout));
  divi divi_1 (.dividend(a), .divisor(b), .clk(clk), .done(done), .quotient(diiv[31:0]), .remainder(diiv[63:32]));
  ROTATE rotate_1 (.a(a), .b(b), .ouuut(ROTR));
  clooo clooo_1 (.A(a), .OUTTTT(CLOO));
  clooo clooo_2 (.A(not_2_out), .OUTTTT(CLZ));
  Multiplexer #(.select(4), .width(64)) multiplexer_1 (
    .in0({{31{1'b0}}, ADD}), .in1(SUB), .in2(MUL), .in3(diiv), .in4({{32{1'b0}}, Annd}),
    .in5({{32{1'b0}}, oor}), .in6({{32{1'b0}}, xoor}), .in7(CLOO), .in8(CLZ), .in9(SLL11), .in10(SRL1),
    .in11(SRA1), .in12(ROTR), .out(multiplexer_1_out), .sel(aluop));  // open: in13, in14, in15
  Multiplexer #(.width(32)) multiplexer_2 (.in0({32{1'b1}}), .in1({32{1'b0}}), .out(SUB[63:32]), .sel(csa_2_cout));
  Multiplexer #(.width(64)) multiplexer_3 (
    .in0(multiplexer_1_out), .in1(not_3_out), .out(multiplexer_3_out), .sel(output_inverted));
  assign not_3_out = ~multiplexer_1_out;  // NOT_Gate not_3, 64 bits wide
  Adder #(.width(64)) adder_1 (
    .a({64{1'b0}}), .b(multiplexer_3_out), .out(adder_1_out), .cin(output_inc));  // open: cout
  SRL2 srl2_1 (.a(a), .b(b), .output1(SRL1));
  SRA11 sra11_1 (.a(a), .b(b), .output1(SRA1));
  Register #(.width(32)) register_1 (.D(adder_1_out[31:0]), .en(1'b1), .clk(clk), .Q(res_low));  // open: clr
  Register #(.width(32)) register_2 (.D(adder_1_out[63:32]), .en(1'b1), .clk(clk), .Q(res_high));  // open: clr
  assign oor = a | b;  // OR_Gate or_1, 32 bits wide
  assign xoor = a ^ b;  // XOR_Gate xor_1, 32 bits wide
  SLL1 sll1_1 (.a(a), .b(b), .output1(SLL11));
  assign Annd = a & b;  // AND_Gate and_1, 32 bits wide
  mul11 mul11_1 (.b(b), .a(a), .mul_out(MUL));

  // Notes on the sheet:
  //   aluop: initial=0x9
  //   a: initial=0x45b352
endmodule

module CSA (
  input  cin,
  input  [31:0] A,
  input  [31:0] B,
  output [31:0] SUM,
  output cout
);

  wire adder_1_cout, adder_2_cout, adder_3_cout, adder_4_cout, adder_5_cout, adder_6_cout, adder_7_cout,
       multiplexer_2_out, multiplexer_4_out;
  wire [7:0] adder_2_out, adder_3_out, adder_4_out, adder_5_out, adder_6_out, adder_7_out;

  Adder adder_1 (.a(A[7:0]), .b(B[7:0]), .out(SUM[7:0]), .cin(cin), .cout(adder_1_cout));
  Adder adder_2 (.a(A[15:8]), .b(B[15:8]), .out(adder_2_out), .cout(adder_2_cout));  // open: cin
  Adder adder_3 (.a(A[15:8]), .b(B[15:8]), .out(adder_3_out), .cin(1'b1), .cout(adder_3_cout));
  Adder adder_4 (.a(A[23:16]), .b(B[23:16]), .out(adder_4_out), .cout(adder_4_cout));  // open: cin
  Adder adder_5 (.a(A[23:16]), .b(B[23:16]), .out(adder_5_out), .cin(1'b1), .cout(adder_5_cout));
  Adder adder_6 (.a(A[31:24]), .b(B[31:24]), .out(adder_6_out), .cout(adder_6_cout));  // open: cin
  Adder adder_7 (.a(A[31:24]), .b(B[31:24]), .out(adder_7_out), .cin(1'b1), .cout(adder_7_cout));
  Multiplexer #(.width(8)) multiplexer_1 (.in0(adder_2_out), .in1(adder_3_out), .out(SUM[15:8]), .sel(adder_1_cout));
  Multiplexer multiplexer_2 (.in0(adder_2_cout), .in1(adder_3_cout), .out(multiplexer_2_out), .sel(adder_1_cout));
  Multiplexer #(.width(8)) multiplexer_3 (
    .in0(adder_4_out), .in1(adder_5_out), .out(SUM[23:16]), .sel(multiplexer_2_out));
  Multiplexer multiplexer_4 (.in0(adder_4_cout), .in1(adder_5_cout), .out(multiplexer_4_out), .sel(multiplexer_2_out));
  Multiplexer #(.width(8)) multiplexer_5 (
    .in0(adder_6_out), .in1(adder_7_out), .out(SUM[31:24]), .sel(multiplexer_4_out));
  Multiplexer multiplexer_6 (.in0(adder_6_cout), .in1(adder_7_cout), .out(cout), .sel(multiplexer_4_out));
endmodule

module SRL2 (
  input  [31:0] a,
  input  [31:0] b,
  output [63:0] output1
);

  wire comparator_1_eq;
  wire [4:0] subtractor_1_out;
  wire [26:0] subtractor_1_out_2;
  wire [63:0] multiplexer_1_out, shifter_1_out, shifter_2_out, shifter_3_out;

  Shifter #(.shift("lr"), .width(64)) shifter_1 (.in({{32{1'b0}}, a}), .\dist (6'b000001), .out(shifter_1_out));
  Subtractor #(.width(32)) subtractor_1 (
    .a(b), .b(32'h1), .out({subtractor_1_out_2, subtractor_1_out}));  // open: bin, bout
  Shifter #(.shift("lr"), .width(64)) shifter_2 (
    .in(shifter_1_out), .\dist ({1'b0, subtractor_1_out}), .out(shifter_2_out));
  Shifter #(.shift("lr"), .width(64)) shifter_3 (.in({{32{1'b0}}, a}), .\dist ({1'b0, b[4:0]}), .out(shifter_3_out));
  Multiplexer #(.width(64)) multiplexer_1 (
    .in0(shifter_2_out), .in1(shifter_3_out), .out(multiplexer_1_out), .sel(b[0]));
  Comparator #(.width(5)) comparator_1 (.a(b[4:0]), .b({5{1'b0}}), .eq(comparator_1_eq));  // open: gt, lt
  Multiplexer #(.width(64)) multiplexer_2 (
    .in0(multiplexer_1_out), .in1({{32{1'b0}}, a}), .out(output1), .sel(comparator_1_eq));
endmodule

module SRA11 (
  input  [31:0] a,
  input  [31:0] b,
  output [63:0] output1
);

  wire comparator_2_eq;
  wire [4:0] bit_extender_2_out;
  wire [5:0] subtractor_1_out;
  wire [25:0] subtractor_1_out_2;
  wire [31:0] undriven, undriven_2;
  wire [63:0] bit_extender_1_out, multiplexer_1_out, shifter_1_out, shifter_2_out, shifter_3_out;
  wire [63:32] multiplexer_3_out;

  Comparator #(.width(32)) comparator_1 (.a(undriven), .b(undriven_2));  // open: gt, eq, lt
  assign bit_extender_1_out = {{32{a[31]}}, a};  // Bit_Extender bit_extender_1
  Bit_Extender #(.in_width(32), .out_width(5), .\type ("zero")) bit_extender_2 (.in(b), .out(bit_extender_2_out));
  Shifter #(.shift("lr"), .width(64)) shifter_1 (.in(bit_extender_1_out), .\dist (6'b000001), .out(shifter_1_out));
  Subtractor #(.width(32)) subtractor_1 (
    .a({{27{1'b0}}, bit_extender_2_out}), .b(32'h1), .out({subtractor_1_out_2, subtractor_1_out}));  // open: bin, bout
  Shifter #(.shift("lr"), .width(64)) shifter_2 (.in(shifter_1_out), .\dist (subtractor_1_out), .out(shifter_2_out));
  Shifter #(.shift("lr"), .width(64)) shifter_3 (
    .in(bit_extender_1_out), .\dist ({1'b0, bit_extender_2_out}), .out(shifter_3_out));
  Multiplexer #(.width(64)) multiplexer_1 (
    .in0(shifter_2_out), .in1(shifter_3_out), .out(multiplexer_1_out), .sel(bit_extender_2_out[0]));
  Comparator #(.mode("unsigned"), .width(6)) comparator_2 (
    .a({1'b0, bit_extender_2_out}), .b({6{1'b0}}), .eq(comparator_2_eq));  // open: gt, lt
  Multiplexer #(.width(32)) multiplexer_2 (.in0({32{1'b0}}), .in1({32{1'b1}}), .out(output1[63:32]), .sel(output1[31]));
  Multiplexer #(.width(64)) multiplexer_3 (
    .in0(multiplexer_1_out), .in1(bit_extender_1_out), .out({multiplexer_3_out, output1[31:0]}),
    .sel(comparator_2_eq));
endmodule

module ROTATE (
  input  [31:0] a,
  input  [31:0] b,
  output [63:0] ouuut
);

  wire [31:0] subtractor_1_out;
  wire [63:0] sll1_1_output1, srl2_1_output1;
  wire [63:32] or_1_out;

  Subtractor #(.width(32)) subtractor_1 (.a(32'h20), .b(b), .out(subtractor_1_out));  // open: bin, bout
  SRL2 srl2_1 (.a(a), .b(b), .output1(srl2_1_output1));
  SLL1 sll1_1 (.a(a), .b(subtractor_1_out), .output1(sll1_1_output1));
  assign {or_1_out, ouuut[31:0]} = srl2_1_output1 | sll1_1_output1;  // OR_Gate or_1, 64 bits wide

  assign ouuut[63:32] = {32{1'b0}};
endmodule

module mul11 (
  input  [31:0] b,
  input  [31:0] a,
  output [63:0] mul_out
);

  wire [63:0] csavea_1_sum, csavea_2_sum, csavea_3_sum, csavea_4_sum, csavea_5_sum, csavea_6_sum,
       csavea_7_sum, csavea_8_sum, csavea_9_sum, csavea_10_sum, csavea_11_sum, csavea_12_sum, csavea_13_sum,
       csavea_14_sum, csavea_15_sum, csavea_16_sum, multiplexer_1_out, multiplexer_2_out, multiplexer_3_out,
       multiplexer_4_out, multiplexer_5_out, multiplexer_6_out, multiplexer_7_out, multiplexer_8_out,
       multiplexer_9_out, multiplexer_10_out, multiplexer_11_out, multiplexer_12_out, multiplexer_13_out,
       multiplexer_14_out, multiplexer_15_out, multiplexer_16_out, multiplexer_17_out, multiplexer_18_out,
       multiplexer_19_out, multiplexer_20_out, multiplexer_21_out, multiplexer_22_out, multiplexer_23_out,
       multiplexer_24_out, multiplexer_25_out, multiplexer_26_out, multiplexer_27_out, multiplexer_28_out,
       multiplexer_29_out, multiplexer_30_out, multiplexer_31_out, multiplexer_32_out, sll1_1_output1,
       sll1_2_output1, sll1_3_output1, sll1_4_output1, sll1_5_output1, sll1_6_output1, sll1_7_output1,
       sll1_8_output1, sll1_9_output1, sll1_10_output1, sll1_11_output1, sll1_12_output1, sll1_13_output1,
       sll1_14_output1, sll1_15_output1, sll1_16_output1, sll1_17_output1, sll1_18_output1, sll1_19_output1,
       sll1_20_output1, sll1_21_output1, sll1_22_output1, sll1_23_output1, sll1_24_output1, sll1_25_output1,
       sll1_26_output1, sll1_27_output1, sll1_28_output1, sll1_29_output1, sll1_30_output1, sll1_31_output1,
       sll1_32_output1;

  SLL1 sll1_1 (.a(a), .b({32{1'b0}}), .output1(sll1_1_output1));
  SLL1 sll1_2 (.a(a), .b(32'h1), .output1(sll1_2_output1));
  SLL1 sll1_3 (.a(a), .b(32'h2), .output1(sll1_3_output1));
  SLL1 sll1_4 (.a(a), .b(32'h3), .output1(sll1_4_output1));
  SLL1 sll1_5 (.a(a), .b(32'h4), .output1(sll1_5_output1));
  SLL1 sll1_6 (.a(a), .b(32'h5), .output1(sll1_6_output1));
  SLL1 sll1_7 (.a(a), .b(32'h6), .output1(sll1_7_output1));
  SLL1 sll1_8 (.a(a), .b(32'h7), .output1(sll1_8_output1));
  SLL1 sll1_9 (.a(a), .b(32'h8), .output1(sll1_9_output1));
  SLL1 sll1_10 (.a(a), .b(32'h9), .output1(sll1_10_output1));
  SLL1 sll1_11 (.a(a), .b(32'ha), .output1(sll1_11_output1));
  SLL1 sll1_12 (.a(a), .b(32'hb), .output1(sll1_12_output1));
  SLL1 sll1_13 (.a(a), .b(32'hc), .output1(sll1_13_output1));
  SLL1 sll1_14 (.a(a), .b(32'hd), .output1(sll1_14_output1));
  SLL1 sll1_15 (.a(a), .b(32'he), .output1(sll1_15_output1));
  SLL1 sll1_16 (.a(a), .b(32'hf), .output1(sll1_16_output1));
  SLL1 sll1_17 (.a(a), .b(32'h10), .output1(sll1_17_output1));
  SLL1 sll1_18 (.a(a), .b(32'h11), .output1(sll1_18_output1));
  SLL1 sll1_19 (.a(a), .b(32'h12), .output1(sll1_19_output1));
  SLL1 sll1_20 (.a(a), .b(32'h13), .output1(sll1_20_output1));
  SLL1 sll1_21 (.a(a), .b(32'h14), .output1(sll1_21_output1));
  SLL1 sll1_22 (.a(a), .b(32'h15), .output1(sll1_22_output1));
  SLL1 sll1_23 (.a(a), .b(32'h16), .output1(sll1_23_output1));
  SLL1 sll1_24 (.a(a), .b(32'h17), .output1(sll1_24_output1));
  SLL1 sll1_25 (.a(a), .b(32'h18), .output1(sll1_25_output1));
  SLL1 sll1_26 (.a(a), .b(32'h19), .output1(sll1_26_output1));
  SLL1 sll1_27 (.a(a), .b(32'h1a), .output1(sll1_27_output1));
  SLL1 sll1_28 (.a(a), .b(32'h1b), .output1(sll1_28_output1));
  SLL1 sll1_29 (.a(a), .b(32'h1c), .output1(sll1_29_output1));
  SLL1 sll1_30 (.a(a), .b(32'h1d), .output1(sll1_30_output1));
  SLL1 sll1_31 (.a(a), .b(32'h1e), .output1(sll1_31_output1));
  SLL1 sll1_32 (.a(a), .b(32'h1f), .output1(sll1_32_output1));
  Multiplexer #(.width(64)) multiplexer_1 (.in0({64{1'b0}}), .in1(sll1_1_output1), .out(multiplexer_1_out), .sel(b[0]));
  Multiplexer #(.width(64)) multiplexer_2 (.in0({64{1'b0}}), .in1(sll1_2_output1), .out(multiplexer_2_out), .sel(b[1]));
  Multiplexer #(.width(64)) multiplexer_3 (.in0({64{1'b0}}), .in1(sll1_3_output1), .out(multiplexer_3_out), .sel(b[2]));
  Multiplexer #(.width(64)) multiplexer_4 (.in0({64{1'b0}}), .in1(sll1_4_output1), .out(multiplexer_4_out), .sel(b[3]));
  Multiplexer #(.width(64)) multiplexer_5 (.in0({64{1'b0}}), .in1(sll1_5_output1), .out(multiplexer_5_out), .sel(b[4]));
  Multiplexer #(.width(64)) multiplexer_6 (.in0({64{1'b0}}), .in1(sll1_6_output1), .out(multiplexer_6_out), .sel(b[5]));
  Multiplexer #(.width(64)) multiplexer_7 (.in0({64{1'b0}}), .in1(sll1_7_output1), .out(multiplexer_7_out), .sel(b[6]));
  Multiplexer #(.width(64)) multiplexer_8 (.in0({64{1'b0}}), .in1(sll1_8_output1), .out(multiplexer_8_out), .sel(b[7]));
  Multiplexer #(.width(64)) multiplexer_9 (.in0({64{1'b0}}), .in1(sll1_9_output1), .out(multiplexer_9_out), .sel(b[8]));
  Multiplexer #(.width(64)) multiplexer_10 (
    .in0({64{1'b0}}), .in1(sll1_10_output1), .out(multiplexer_10_out), .sel(b[9]));
  Multiplexer #(.width(64)) multiplexer_11 (
    .in0({64{1'b0}}), .in1(sll1_11_output1), .out(multiplexer_11_out), .sel(b[10]));
  Multiplexer #(.width(64)) multiplexer_12 (
    .in0({64{1'b0}}), .in1(sll1_12_output1), .out(multiplexer_12_out), .sel(b[11]));
  Multiplexer #(.width(64)) multiplexer_13 (
    .in0({64{1'b0}}), .in1(sll1_13_output1), .out(multiplexer_13_out), .sel(b[12]));
  Multiplexer #(.width(64)) multiplexer_14 (
    .in0({64{1'b0}}), .in1(sll1_14_output1), .out(multiplexer_14_out), .sel(b[13]));
  Multiplexer #(.width(64)) multiplexer_15 (
    .in0({64{1'b0}}), .in1(sll1_15_output1), .out(multiplexer_15_out), .sel(b[14]));
  Multiplexer #(.width(64)) multiplexer_16 (
    .in0({64{1'b0}}), .in1(sll1_16_output1), .out(multiplexer_16_out), .sel(b[15]));
  Multiplexer #(.width(64)) multiplexer_17 (
    .in0({64{1'b0}}), .in1(sll1_17_output1), .out(multiplexer_17_out), .sel(b[16]));
  Multiplexer #(.width(64)) multiplexer_18 (
    .in0({64{1'b0}}), .in1(sll1_18_output1), .out(multiplexer_18_out), .sel(b[17]));
  Multiplexer #(.width(64)) multiplexer_19 (
    .in0({64{1'b0}}), .in1(sll1_19_output1), .out(multiplexer_19_out), .sel(b[18]));
  Multiplexer #(.width(64)) multiplexer_20 (
    .in0({64{1'b0}}), .in1(sll1_20_output1), .out(multiplexer_20_out), .sel(b[19]));
  Multiplexer #(.width(64)) multiplexer_21 (
    .in0({64{1'b0}}), .in1(sll1_21_output1), .out(multiplexer_21_out), .sel(b[20]));
  Multiplexer #(.width(64)) multiplexer_22 (
    .in0({64{1'b0}}), .in1(sll1_22_output1), .out(multiplexer_22_out), .sel(b[21]));
  Multiplexer #(.width(64)) multiplexer_23 (
    .in0({64{1'b0}}), .in1(sll1_23_output1), .out(multiplexer_23_out), .sel(b[22]));
  Multiplexer #(.width(64)) multiplexer_24 (
    .in0({64{1'b0}}), .in1(sll1_24_output1), .out(multiplexer_24_out), .sel(b[23]));
  Multiplexer #(.width(64)) multiplexer_25 (
    .in0({64{1'b0}}), .in1(sll1_25_output1), .out(multiplexer_25_out), .sel(b[24]));
  Multiplexer #(.width(64)) multiplexer_26 (
    .in0({64{1'b0}}), .in1(sll1_26_output1), .out(multiplexer_26_out), .sel(b[25]));
  Multiplexer #(.width(64)) multiplexer_27 (
    .in0({64{1'b0}}), .in1(sll1_27_output1), .out(multiplexer_27_out), .sel(b[26]));
  Multiplexer #(.width(64)) multiplexer_28 (
    .in0({64{1'b0}}), .in1(sll1_28_output1), .out(multiplexer_28_out), .sel(b[27]));
  Multiplexer #(.width(64)) multiplexer_29 (
    .in0({64{1'b0}}), .in1(sll1_29_output1), .out(multiplexer_29_out), .sel(b[28]));
  Multiplexer #(.width(64)) multiplexer_30 (
    .in0({64{1'b0}}), .in1(sll1_30_output1), .out(multiplexer_30_out), .sel(b[29]));
  Multiplexer #(.width(64)) multiplexer_31 (
    .in0({64{1'b0}}), .in1(sll1_31_output1), .out(multiplexer_31_out), .sel(b[30]));
  Multiplexer #(.width(64)) multiplexer_32 (
    .in0({64{1'b0}}), .in1(sll1_32_output1), .out(multiplexer_32_out), .sel(b[31]));
  CSaveA csavea_1 (.a(multiplexer_1_out), .b(multiplexer_2_out), .c(multiplexer_3_out), .sum(csavea_1_sum));
  CSaveA csavea_2 (.a(multiplexer_4_out), .b(multiplexer_5_out), .c(multiplexer_6_out), .sum(csavea_2_sum));
  CSaveA csavea_3 (.a(multiplexer_7_out), .b(multiplexer_8_out), .c(multiplexer_9_out), .sum(csavea_3_sum));
  CSaveA csavea_4 (.a(multiplexer_10_out), .b(multiplexer_11_out), .c(multiplexer_12_out), .sum(csavea_4_sum));
  CSaveA csavea_5 (.a(multiplexer_13_out), .b(multiplexer_14_out), .c(multiplexer_15_out), .sum(csavea_5_sum));
  CSaveA csavea_6 (.a(multiplexer_16_out), .b(multiplexer_17_out), .c(multiplexer_18_out), .sum(csavea_6_sum));
  CSaveA csavea_7 (.a(multiplexer_19_out), .b(multiplexer_20_out), .c(multiplexer_21_out), .sum(csavea_7_sum));
  CSaveA csavea_8 (.a(multiplexer_22_out), .b(multiplexer_23_out), .c(multiplexer_24_out), .sum(csavea_8_sum));
  CSaveA csavea_9 (.a(multiplexer_25_out), .b(multiplexer_26_out), .c(multiplexer_27_out), .sum(csavea_9_sum));
  CSaveA csavea_10 (.a(multiplexer_28_out), .b(multiplexer_29_out), .c(multiplexer_30_out), .sum(csavea_10_sum));
  CSaveA csavea_11 (.a(multiplexer_31_out), .b(multiplexer_32_out), .c({64{1'b0}}), .sum(csavea_11_sum));
  CSaveA csavea_12 (.a(csavea_1_sum), .b(csavea_2_sum), .c(csavea_3_sum), .sum(csavea_12_sum));
  CSaveA csavea_13 (.a(csavea_4_sum), .b(csavea_5_sum), .c(csavea_6_sum), .sum(csavea_13_sum));
  CSaveA csavea_14 (.a(csavea_7_sum), .b(csavea_8_sum), .c(csavea_9_sum), .sum(csavea_14_sum));
  CSaveA csavea_15 (.a(csavea_10_sum), .b(csavea_11_sum), .c({64{1'b0}}), .sum(csavea_15_sum));
  CSaveA csavea_16 (.a(csavea_12_sum), .b(csavea_13_sum), .c(csavea_14_sum), .sum(csavea_16_sum));
  CSaveA csavea_17 (.a(csavea_16_sum), .b(csavea_15_sum), .c({64{1'b0}}), .sum(mul_out));
endmodule

module divi (
  input  [31:0] dividend,
  input  [31:0] divisor,
  input  clk,
  output done,
  output [31:0] quotient,
  output [31:0] remainder
);

  wire comparator_1_eq, comparator_2_eq, comparator_3_lt, hi, not_1_out, not_2_out, or_1_out;
  wire [0:0] q_reg_q_2;
  wire [30:0] multiplexer_3_out;
  wire [31:0] a_reg_q, multiplexer_2_out, register_1_q, register_2_q, subtractor_2_out;
  wire [31:1] q_reg_q;
  wire [31:31] multiplexer_3_out_2;
  wire [63:0] counter_q, multiplexer_1_out, subtractor_1_out;

  Register #(.width(32)) register_1 (.D(dividend), .en(1'b1), .clk(clk), .Q(register_1_q));  // open: clr
  Comparator #(.mode("unsigned"), .width(32)) comparator_1 (
    .a(dividend), .b(register_1_q), .eq(comparator_1_eq));  // open: gt, lt
  Register #(.width(32)) register_2 (.D(divisor), .en(1'b1), .clk(clk), .Q(register_2_q));  // open: clr
  not not_1 (not_1_out, comparator_1_eq);
  or or_1 (or_1_out, not_1_out, not_2_out);
  Comparator #(.mode("unsigned"), .width(32)) comparator_2 (
    .a(divisor), .b(register_2_q), .eq(comparator_2_eq));  // open: gt, lt
  Register #(.width(64)) counter (.D(multiplexer_1_out), .en(1'b1), .clk(clk), .Q(counter_q), .clr(1'b0));
  Multiplexer #(.width(64)) multiplexer_1 (
    .in0(subtractor_1_out), .in1(64'h20), .out(multiplexer_1_out), .sel(or_1_out));
  not not_2 (not_2_out, comparator_2_eq);
  Register #(.width(32)) q_reg (.D(multiplexer_2_out), .en(1'b1), .clk(clk), .Q({q_reg_q_2[0], q_reg_q}), .clr(1'b0));
  Multiplexer #(.width(32)) multiplexer_2 (
    .in0({q_reg_q, hi}), .in1(dividend), .out(multiplexer_2_out), .sel(or_1_out));
  Register #(.width(32)) a_reg (
    .D({multiplexer_3_out, q_reg_q_2[0]}), .en(1'b1), .clk(clk), .Q(a_reg_q), .clr(or_1_out));
  Subtractor #(.width(64)) subtractor_1 (.a(counter_q), .b(64'h1), .out(subtractor_1_out), .bin(1'b0));  // open: bout
  Multiplexer #(.width(32)) multiplexer_3 (
    .in0(a_reg_q), .in1(subtractor_2_out), .out({multiplexer_3_out_2[31], multiplexer_3_out}), .sel(hi));
  Subtractor #(.width(32)) subtractor_2 (.a(a_reg_q), .b(divisor), .out(subtractor_2_out), .bin(1'b0));  // open: bout
  Comparator #(.mode("unsigned"), .width(32)) comparator_3 (
    .a(a_reg_q), .b(divisor), .lt(comparator_3_lt));  // open: gt, eq
  not not_3 (hi, comparator_3_lt);
  Comparator #(.mode("unsigned"), .width(64)) comparator_4 (.a(counter_q), .b({64{1'b0}}), .eq(done));  // open: gt, lt
  Register #(.width(32)) register_3 (.D({q_reg_q, hi}), .en(done), .clk(clk), .Q(quotient), .clr(or_1_out));
  Register #(.width(32)) register_4 (
    .D({multiplexer_3_out_2[31], multiplexer_3_out}), .en(done), .clk(clk), .Q(remainder), .clr(or_1_out));
endmodule

module SLL1 (
  input  [31:0] a,
  input  [31:0] b,
  output [63:0] output1
);

  wire comparator_1_eq;
  wire [4:0] subtractor_1_out;
  wire [26:0] subtractor_1_out_2;
  wire [63:0] multiplexer_1_out, shifter_1_out, shifter_2_out, shifter_3_out;

  Shifter #(.width(64)) shifter_1 (.in({{32{1'b0}}, a}), .\dist (6'b000001), .out(shifter_1_out));
  Subtractor #(.width(32)) subtractor_1 (
    .a(b), .b(32'h1), .out({subtractor_1_out_2, subtractor_1_out}));  // open: bin, bout
  Shifter #(.width(64)) shifter_2 (.in(shifter_1_out), .\dist ({1'b0, subtractor_1_out}), .out(shifter_2_out));
  Shifter #(.width(64)) shifter_3 (.in({{32{1'b0}}, a}), .\dist ({1'b0, b[4:0]}), .out(shifter_3_out));
  Multiplexer #(.width(64)) multiplexer_1 (
    .in0(shifter_2_out), .in1(shifter_3_out), .out(multiplexer_1_out), .sel(b[0]));
  Comparator #(.width(5)) comparator_1 (.a(b[4:0]), .b({5{1'b0}}), .eq(comparator_1_eq));  // open: gt, lt
  Multiplexer #(.width(64)) multiplexer_2 (
    .in0(multiplexer_1_out), .in1({{32{1'b0}}, a}), .out(output1), .sel(comparator_1_eq));
endmodule

module clooo (
  input  [31:0] A,
  output [63:0] OUTTTT
);

  wire and_1_out, and_2_out, and_3_out, and_4_out, and_5_out, and_6_out, and_7_out, and_8_out, and_9_out,
       and_10_out, and_11_out, and_12_out, and_13_out, and_14_out, and_15_out, and_16_out, and_17_out,
       and_18_out, and_19_out, and_20_out, and_21_out, and_22_out, and_23_out, and_24_out, and_25_out,
       and_26_out, and_27_out, and_28_out, and_29_out, and_30_out, and_31_out, and_32_out;
  wire [1:0] adder_1_out, adder_2_out, adder_3_out, adder_4_out, adder_5_out, adder_6_out, adder_8_out,
       adder_9_out, adder_10_out, adder_11_out, adder_12_out, adder_13_out;
  wire [2:0] adder_14_out;
  wire [2:2] adder_3_cout, adder_6_cout, adder_10_cout, adder_13_cout;
  wire [3:0] adder_7_out, adder_15_out;
  wire [3:3] adder_14_cout;
  wire [4:4] adder_15_cout;

  and and_1 (and_1_out, A[30], and_2_out);
  and and_2 (and_2_out, A[31], 1'b1);
  and and_3 (and_3_out, A[29], and_1_out);
  Adder #(.width(1)) adder_1 (
    .a(and_1_out), .b(and_2_out), .out(adder_1_out[0]), .cin(and_3_out), .cout(adder_1_out[1]));
  and and_4 (and_4_out, A[27], and_5_out);
  and and_5 (and_5_out, A[28], and_3_out);
  and and_6 (and_6_out, A[26], and_4_out);
  Adder #(.width(1)) adder_2 (
    .a(and_4_out), .b(and_5_out), .out(adder_2_out[0]), .cin(and_6_out), .cout(adder_2_out[1]));
  and and_7 (and_7_out, A[24], and_8_out);
  and and_8 (and_8_out, A[25], and_6_out);
  Adder #(.width(2)) adder_3 (
    .a(adder_2_out), .b(adder_1_out), .out(adder_3_out), .cin(and_8_out), .cout(adder_3_cout[2]));
  and and_9 (and_9_out, A[22], and_10_out);
  and and_10 (and_10_out, A[23], and_7_out);
  and and_11 (and_11_out, A[21], and_9_out);
  Adder #(.width(1)) adder_4 (
    .a(and_10_out), .b(and_7_out), .out(adder_4_out[0]), .cin(and_9_out), .cout(adder_4_out[1]));
  and and_12 (and_12_out, A[19], and_13_out);
  and and_13 (and_13_out, A[20], and_11_out);
  Adder #(.width(1)) adder_5 (
    .a(and_13_out), .b(and_11_out), .out(adder_5_out[0]), .cin(and_12_out), .cout(adder_5_out[1]));
  and and_14 (and_14_out, A[18], and_12_out);
  Adder #(.width(2)) adder_6 (
    .a(adder_5_out), .b(adder_4_out), .out(adder_6_out), .cin(and_14_out), .cout(adder_6_cout[2]));
  and and_15 (and_15_out, A[16], and_16_out);
  and and_16 (and_16_out, A[17], and_14_out);
  Adder #(.width(3)) adder_7 (
    .a({adder_6_cout[2], adder_6_out}), .b({adder_3_cout[2], adder_3_out}), .out(adder_7_out[2:0]),
    .cin(and_16_out), .cout(adder_7_out[3]));
  and and_17 (and_17_out, A[14], and_18_out);
  and and_18 (and_18_out, A[15], and_15_out);
  and and_19 (and_19_out, A[13], and_17_out);
  Adder #(.width(1)) adder_8 (
    .a(and_18_out), .b(and_15_out), .out(adder_8_out[0]), .cin(and_17_out), .cout(adder_8_out[1]));
  and and_20 (and_20_out, A[11], and_21_out);
  and and_21 (and_21_out, A[12], and_19_out);
  Adder #(.width(1)) adder_9 (
    .a(and_21_out), .b(and_19_out), .out(adder_9_out[0]), .cin(and_20_out), .cout(adder_9_out[1]));
  and and_22 (and_22_out, A[10], and_20_out);
  Adder #(.width(2)) adder_10 (
    .a(adder_9_out), .b(adder_8_out), .out(adder_10_out), .cin(and_22_out), .cout(adder_10_cout[2]));
  and and_23 (and_23_out, A[8], and_24_out);
  and and_24 (and_24_out, A[9], and_22_out);
  and and_25 (and_25_out, A[6], and_26_out);
  and and_26 (and_26_out, A[7], and_23_out);
  Adder #(.width(1)) adder_11 (
    .a(and_23_out), .b(and_24_out), .out(adder_11_out[0]), .cin(and_26_out), .cout(adder_11_out[1]));
  and and_27 (and_27_out, A[5], and_25_out);
  and and_28 (and_28_out, A[3], and_29_out);
  and and_29 (and_29_out, A[4], and_27_out);
  Adder #(.width(1)) adder_12 (
    .a(and_27_out), .b(and_25_out), .out(adder_12_out[0]), .cin(and_29_out), .cout(adder_12_out[1]));
  and and_30 (and_30_out, A[2], and_28_out);
  Adder #(.width(2)) adder_13 (
    .a(adder_12_out), .b(adder_11_out), .out(adder_13_out), .cin(and_28_out), .cout(adder_13_cout[2]));
  Adder #(.width(3)) adder_14 (
    .a({adder_13_cout[2], adder_13_out}), .b({adder_10_cout[2], adder_10_out}), .out(adder_14_out),
    .cin(and_30_out), .cout(adder_14_cout[3]));
  and and_31 (and_31_out, A[0], and_32_out);
  and and_32 (and_32_out, A[1], and_30_out);
  Adder #(.width(4)) adder_15 (
    .a({adder_14_cout[3], adder_14_out}), .b(adder_7_out), .out(adder_15_out), .cin(and_32_out),
    .cout(adder_15_cout[4]));
  Adder #(.width(64)) adder_16 (
    .a({64{1'b0}}), .b({{59{1'b0}}, adder_15_cout[4], adder_15_out}), .out(OUTTTT), .cin(and_31_out));  // open: cout
endmodule

module srlf (
  input  [63:0] a,
  input  [31:0] b,
  output [63:0] output1
);

  wire comparator_1_eq;
  wire [4:0] subtractor_1_out;
  wire [26:0] subtractor_1_out_2;
  wire [63:0] multiplexer_1_out, shifter_1_out, shifter_2_out, shifter_3_out;

  Shifter #(.shift("lr"), .width(64)) shifter_1 (.in(a), .\dist (6'b000001), .out(shifter_1_out));
  Subtractor #(.width(32)) subtractor_1 (
    .a(b), .b(32'h1), .out({subtractor_1_out_2, subtractor_1_out}));  // open: bin, bout
  Shifter #(.shift("lr"), .width(64)) shifter_2 (
    .in(shifter_1_out), .\dist ({1'b0, subtractor_1_out}), .out(shifter_2_out));
  Shifter #(.shift("lr"), .width(64)) shifter_3 (.in(a), .\dist ({1'b0, b[4:0]}), .out(shifter_3_out));
  Multiplexer #(.width(64)) multiplexer_1 (
    .in0(shifter_2_out), .in1(shifter_3_out), .out(multiplexer_1_out), .sel(b[0]));
  Comparator #(.width(32)) comparator_1 (.a(b), .b({32{1'b0}}), .eq(comparator_1_eq));  // open: gt, lt
  Multiplexer #(.width(64)) multiplexer_2 (.in0(multiplexer_1_out), .in1(a), .out(output1), .sel(comparator_1_eq));
endmodule

module sllf (
  input  [63:0] a,
  input  [31:0] b,
  output [63:0] output1
);

  wire comparator_1_eq;
  wire [5:0] subtractor_1_out;
  wire [25:0] subtractor_1_out_2;
  wire [63:0] multiplexer_1_out, shifter_1_out, shifter_2_out, shifter_3_out;

  Shifter #(.width(64)) shifter_1 (.in(a), .\dist (6'b000001), .out(shifter_1_out));
  Subtractor #(.width(32)) subtractor_1 (
    .a(b), .b(32'h1), .out({subtractor_1_out_2, subtractor_1_out}));  // open: bin, bout
  Shifter #(.width(64)) shifter_2 (.in(shifter_1_out), .\dist (subtractor_1_out), .out(shifter_2_out));
  Shifter #(.width(64)) shifter_3 (.in(a), .\dist (b[5:0]), .out(shifter_3_out));
  Multiplexer #(.width(64)) multiplexer_1 (
    .in0(shifter_2_out), .in1(shifter_3_out), .out(multiplexer_1_out), .sel(b[0]));
  Comparator #(.width(32)) comparator_1 (.a(b), .b({32{1'b0}}), .eq(comparator_1_eq));  // open: gt, lt
  Multiplexer #(.width(64)) multiplexer_2 (.in0(multiplexer_1_out), .in1(a), .out(output1), .sel(comparator_1_eq));
endmodule

module CSaveA (
  input  [63:0] a,
  input  [63:0] b,
  input  [63:0] c,
  output [63:0] sum
);

  wire adder_1_cout, adder_1_out, adder_2_cout, adder_2_out, adder_3_cout, adder_3_out, adder_4_cout,
       adder_4_out, adder_5_cout, adder_5_out, adder_6_cout, adder_6_out, adder_7_cout, adder_7_out,
       adder_8_cout, adder_8_out, adder_9_cout, adder_9_out, adder_10_cout, adder_10_out, adder_11_cout,
       adder_11_out, adder_12_cout, adder_12_out, adder_13_cout, adder_13_out, adder_14_cout, adder_14_out,
       adder_15_cout, adder_15_out, adder_16_cout, adder_16_out, adder_17_cout, adder_17_out, adder_18_cout,
       adder_18_out, adder_19_cout, adder_19_out, adder_20_cout, adder_20_out, adder_21_cout, adder_21_out,
       adder_22_cout, adder_22_out, adder_23_cout, adder_23_out, adder_24_cout, adder_24_out, adder_25_cout,
       adder_25_out, adder_26_cout, adder_26_out, adder_27_cout, adder_27_out, adder_28_cout, adder_28_out,
       adder_29_cout, adder_29_out, adder_30_cout, adder_30_out, adder_31_cout, adder_31_out, adder_32_cout,
       adder_32_out, adder_33_cout, adder_33_out, adder_34_cout, adder_34_out, adder_35_cout, adder_35_out,
       adder_36_cout, adder_36_out, adder_37_cout, adder_37_out, adder_38_cout, adder_38_out, adder_39_cout,
       adder_39_out, adder_40_cout, adder_40_out, adder_41_cout, adder_41_out, adder_42_cout, adder_42_out,
       adder_43_cout, adder_43_out, adder_44_cout, adder_44_out, adder_45_cout, adder_45_out, adder_46_cout,
       adder_46_out, adder_47_cout, adder_47_out, adder_48_cout, adder_48_out, adder_49_cout, adder_49_out,
       adder_50_cout, adder_50_out, adder_51_cout, adder_51_out, adder_52_cout, adder_52_out, adder_53_cout,
       adder_53_out, adder_54_cout, adder_54_out, adder_55_cout, adder_55_out, adder_56_cout, adder_56_out,
       adder_57_cout, adder_57_out, adder_58_cout, adder_58_out, adder_59_cout, adder_59_out, adder_60_cout,
       adder_60_out, adder_61_cout, adder_61_out, adder_62_cout, adder_62_out, adder_63_out, adder_64_cout,
       adder_65_cout, adder_66_cout, adder_67_cout, adder_68_cout, adder_69_cout, adder_70_cout,
       adder_71_cout, adder_72_cout, adder_73_cout, adder_74_cout, adder_75_cout, adder_76_cout,
       adder_77_cout, adder_78_cout, adder_79_cout, adder_80_cout, adder_81_cout, adder_82_cout,
       adder_83_cout, adder_84_cout, adder_85_cout, adder_86_cout, adder_87_cout, adder_88_cout,
       adder_89_cout, adder_90_cout, adder_91_cout, adder_92_cout, adder_93_cout, adder_94_cout,
       adder_95_cout, adder_96_cout, adder_97_cout, adder_98_cout, adder_99_cout, adder_100_cout,
       adder_101_cout, adder_102_cout, adder_103_cout, adder_104_cout, adder_105_cout, adder_106_cout,
       adder_107_cout, adder_108_cout, adder_109_cout, adder_110_cout, adder_111_cout, adder_112_cout,
       adder_113_cout, adder_114_cout, adder_115_cout, adder_116_cout, adder_117_cout, adder_118_cout,
       adder_119_cout, adder_120_cout, adder_121_cout, adder_122_cout, adder_123_cout, adder_124_cout,
       adder_125_cout, adder_126_cout;

  Adder #(.width(1)) adder_1 (.a(b[1]), .b(c[1]), .out(adder_1_out), .cin(a[1]), .cout(adder_1_cout));
  Adder #(.width(1)) adder_2 (.a(b[2]), .b(c[2]), .out(adder_2_out), .cin(a[2]), .cout(adder_2_cout));
  Adder #(.width(1)) adder_3 (.a(b[3]), .b(c[3]), .out(adder_3_out), .cin(a[3]), .cout(adder_3_cout));
  Adder #(.width(1)) adder_4 (.a(b[4]), .b(c[4]), .out(adder_4_out), .cin(a[4]), .cout(adder_4_cout));
  Adder #(.width(1)) adder_5 (.a(b[5]), .b(c[5]), .out(adder_5_out), .cin(a[5]), .cout(adder_5_cout));
  Adder #(.width(1)) adder_6 (.a(b[6]), .b(c[6]), .out(adder_6_out), .cin(a[6]), .cout(adder_6_cout));
  Adder #(.width(1)) adder_7 (.a(b[7]), .b(c[7]), .out(adder_7_out), .cin(a[7]), .cout(adder_7_cout));
  Adder #(.width(1)) adder_8 (.a(b[8]), .b(c[8]), .out(adder_8_out), .cin(a[8]), .cout(adder_8_cout));
  Adder #(.width(1)) adder_9 (.a(b[9]), .b(c[9]), .out(adder_9_out), .cin(a[9]), .cout(adder_9_cout));
  Adder #(.width(1)) adder_10 (.a(b[10]), .b(c[10]), .out(adder_10_out), .cin(a[10]), .cout(adder_10_cout));
  Adder #(.width(1)) adder_11 (.a(b[11]), .b(c[11]), .out(adder_11_out), .cin(a[11]), .cout(adder_11_cout));
  Adder #(.width(1)) adder_12 (.a(b[12]), .b(c[12]), .out(adder_12_out), .cin(a[12]), .cout(adder_12_cout));
  Adder #(.width(1)) adder_13 (.a(b[13]), .b(c[13]), .out(adder_13_out), .cin(a[13]), .cout(adder_13_cout));
  Adder #(.width(1)) adder_14 (.a(b[14]), .b(c[14]), .out(adder_14_out), .cin(a[14]), .cout(adder_14_cout));
  Adder #(.width(1)) adder_15 (.a(b[15]), .b(c[15]), .out(adder_15_out), .cin(a[15]), .cout(adder_15_cout));
  Adder #(.width(1)) adder_16 (.a(b[16]), .b(c[16]), .out(adder_16_out), .cin(a[16]), .cout(adder_16_cout));
  Adder #(.width(1)) adder_17 (.a(b[17]), .b(c[17]), .out(adder_17_out), .cin(a[17]), .cout(adder_17_cout));
  Adder #(.width(1)) adder_18 (.a(b[18]), .b(c[18]), .out(adder_18_out), .cin(a[18]), .cout(adder_18_cout));
  Adder #(.width(1)) adder_19 (.a(b[19]), .b(c[19]), .out(adder_19_out), .cin(a[19]), .cout(adder_19_cout));
  Adder #(.width(1)) adder_20 (.a(b[20]), .b(c[20]), .out(adder_20_out), .cin(a[20]), .cout(adder_20_cout));
  Adder #(.width(1)) adder_21 (.a(b[21]), .b(c[21]), .out(adder_21_out), .cin(a[21]), .cout(adder_21_cout));
  Adder #(.width(1)) adder_22 (.a(b[22]), .b(c[22]), .out(adder_22_out), .cin(a[22]), .cout(adder_22_cout));
  Adder #(.width(1)) adder_23 (.a(b[23]), .b(c[23]), .out(adder_23_out), .cin(a[23]), .cout(adder_23_cout));
  Adder #(.width(1)) adder_24 (.a(b[24]), .b(c[24]), .out(adder_24_out), .cin(a[24]), .cout(adder_24_cout));
  Adder #(.width(1)) adder_25 (.a(b[25]), .b(c[25]), .out(adder_25_out), .cin(a[25]), .cout(adder_25_cout));
  Adder #(.width(1)) adder_26 (.a(b[26]), .b(c[26]), .out(adder_26_out), .cin(a[26]), .cout(adder_26_cout));
  Adder #(.width(1)) adder_27 (.a(b[27]), .b(c[27]), .out(adder_27_out), .cin(a[27]), .cout(adder_27_cout));
  Adder #(.width(1)) adder_28 (.a(b[28]), .b(c[28]), .out(adder_28_out), .cin(a[28]), .cout(adder_28_cout));
  Adder #(.width(1)) adder_29 (.a(b[29]), .b(c[29]), .out(adder_29_out), .cin(a[29]), .cout(adder_29_cout));
  Adder #(.width(1)) adder_30 (.a(b[30]), .b(c[30]), .out(adder_30_out), .cin(a[30]), .cout(adder_30_cout));
  Adder #(.width(1)) adder_31 (.a(b[31]), .b(c[31]), .out(adder_31_out), .cin(a[31]), .cout(adder_31_cout));
  Adder #(.width(1)) adder_32 (.a(b[32]), .b(c[32]), .out(adder_32_out), .cin(a[32]), .cout(adder_32_cout));
  Adder #(.width(1)) adder_33 (.a(b[33]), .b(c[33]), .out(adder_33_out), .cin(a[33]), .cout(adder_33_cout));
  Adder #(.width(1)) adder_34 (.a(b[34]), .b(c[34]), .out(adder_34_out), .cin(a[34]), .cout(adder_34_cout));
  Adder #(.width(1)) adder_35 (.a(b[35]), .b(c[35]), .out(adder_35_out), .cin(a[35]), .cout(adder_35_cout));
  Adder #(.width(1)) adder_36 (.a(b[36]), .b(c[36]), .out(adder_36_out), .cin(a[36]), .cout(adder_36_cout));
  Adder #(.width(1)) adder_37 (.a(b[37]), .b(c[37]), .out(adder_37_out), .cin(a[37]), .cout(adder_37_cout));
  Adder #(.width(1)) adder_38 (.a(b[38]), .b(c[38]), .out(adder_38_out), .cin(a[38]), .cout(adder_38_cout));
  Adder #(.width(1)) adder_39 (.a(b[39]), .b(c[39]), .out(adder_39_out), .cin(a[39]), .cout(adder_39_cout));
  Adder #(.width(1)) adder_40 (.a(b[40]), .b(c[40]), .out(adder_40_out), .cin(a[40]), .cout(adder_40_cout));
  Adder #(.width(1)) adder_41 (.a(b[41]), .b(c[41]), .out(adder_41_out), .cin(a[41]), .cout(adder_41_cout));
  Adder #(.width(1)) adder_42 (.a(b[42]), .b(c[42]), .out(adder_42_out), .cin(a[42]), .cout(adder_42_cout));
  Adder #(.width(1)) adder_43 (.a(b[43]), .b(c[43]), .out(adder_43_out), .cin(a[43]), .cout(adder_43_cout));
  Adder #(.width(1)) adder_44 (.a(b[44]), .b(c[44]), .out(adder_44_out), .cin(a[44]), .cout(adder_44_cout));
  Adder #(.width(1)) adder_45 (.a(b[45]), .b(c[45]), .out(adder_45_out), .cin(a[45]), .cout(adder_45_cout));
  Adder #(.width(1)) adder_46 (.a(b[46]), .b(c[46]), .out(adder_46_out), .cin(a[46]), .cout(adder_46_cout));
  Adder #(.width(1)) adder_47 (.a(b[47]), .b(c[47]), .out(adder_47_out), .cin(a[47]), .cout(adder_47_cout));
  Adder #(.width(1)) adder_48 (.a(b[48]), .b(c[48]), .out(adder_48_out), .cin(a[48]), .cout(adder_48_cout));
  Adder #(.width(1)) adder_49 (.a(b[49]), .b(c[49]), .out(adder_49_out), .cin(a[49]), .cout(adder_49_cout));
  Adder #(.width(1)) adder_50 (.a(b[50]), .b(c[50]), .out(adder_50_out), .cin(a[50]), .cout(adder_50_cout));
  Adder #(.width(1)) adder_51 (.a(b[51]), .b(c[51]), .out(adder_51_out), .cin(a[51]), .cout(adder_51_cout));
  Adder #(.width(1)) adder_52 (.a(b[52]), .b(c[52]), .out(adder_52_out), .cin(a[52]), .cout(adder_52_cout));
  Adder #(.width(1)) adder_53 (.a(b[53]), .b(c[53]), .out(adder_53_out), .cin(a[53]), .cout(adder_53_cout));
  Adder #(.width(1)) adder_54 (.a(b[54]), .b(c[54]), .out(adder_54_out), .cin(a[54]), .cout(adder_54_cout));
  Adder #(.width(1)) adder_55 (.a(b[55]), .b(c[55]), .out(adder_55_out), .cin(a[55]), .cout(adder_55_cout));
  Adder #(.width(1)) adder_56 (.a(b[56]), .b(c[56]), .out(adder_56_out), .cin(a[56]), .cout(adder_56_cout));
  Adder #(.width(1)) adder_57 (.a(b[57]), .b(c[57]), .out(adder_57_out), .cin(a[57]), .cout(adder_57_cout));
  Adder #(.width(1)) adder_58 (.a(b[58]), .b(c[58]), .out(adder_58_out), .cin(a[58]), .cout(adder_58_cout));
  Adder #(.width(1)) adder_59 (.a(b[59]), .b(c[59]), .out(adder_59_out), .cin(a[59]), .cout(adder_59_cout));
  Adder #(.width(1)) adder_60 (.a(b[60]), .b(c[60]), .out(adder_60_out), .cin(a[60]), .cout(adder_60_cout));
  Adder #(.width(1)) adder_61 (.a(b[61]), .b(c[61]), .out(adder_61_out), .cin(a[61]), .cout(adder_61_cout));
  Adder #(.width(1)) adder_62 (.a(b[62]), .b(c[62]), .out(adder_62_out), .cin(a[62]), .cout(adder_62_cout));
  Adder #(.width(1)) adder_63 (.a(b[63]), .b(c[63]), .out(adder_63_out), .cin(a[63]));  // open: cout
  Adder #(.width(1)) adder_64 (.a(b[0]), .b(c[0]), .out(sum[0]), .cin(a[0]), .cout(adder_64_cout));
  Adder #(.width(1)) adder_65 (.a(1'b0), .b(adder_1_out), .out(sum[1]), .cin(adder_64_cout), .cout(adder_65_cout));
  Adder #(.width(1)) adder_66 (
    .a(adder_1_cout), .b(adder_2_out), .out(sum[2]), .cin(adder_65_cout), .cout(adder_66_cout));
  Adder #(.width(1)) adder_67 (
    .a(adder_2_cout), .b(adder_3_out), .out(sum[3]), .cin(adder_66_cout), .cout(adder_67_cout));
  Adder #(.width(1)) adder_68 (
    .a(adder_3_cout), .b(adder_4_out), .out(sum[4]), .cin(adder_67_cout), .cout(adder_68_cout));
  Adder #(.width(1)) adder_69 (
    .a(adder_4_cout), .b(adder_5_out), .out(sum[5]), .cin(adder_68_cout), .cout(adder_69_cout));
  Adder #(.width(1)) adder_70 (
    .a(adder_5_cout), .b(adder_6_out), .out(sum[6]), .cin(adder_69_cout), .cout(adder_70_cout));
  Adder #(.width(1)) adder_71 (
    .a(adder_6_cout), .b(adder_7_out), .out(sum[7]), .cin(adder_70_cout), .cout(adder_71_cout));
  Adder #(.width(1)) adder_72 (
    .a(adder_7_cout), .b(adder_8_out), .out(sum[8]), .cin(adder_71_cout), .cout(adder_72_cout));
  Adder #(.width(1)) adder_73 (
    .a(adder_8_cout), .b(adder_9_out), .out(sum[9]), .cin(adder_72_cout), .cout(adder_73_cout));
  Adder #(.width(1)) adder_74 (
    .a(adder_9_cout), .b(adder_10_out), .out(sum[10]), .cin(adder_73_cout), .cout(adder_74_cout));
  Adder #(.width(1)) adder_75 (
    .a(adder_10_cout), .b(adder_11_out), .out(sum[11]), .cin(adder_74_cout), .cout(adder_75_cout));
  Adder #(.width(1)) adder_76 (
    .a(adder_11_cout), .b(adder_12_out), .out(sum[12]), .cin(adder_75_cout), .cout(adder_76_cout));
  Adder #(.width(1)) adder_77 (
    .a(adder_12_cout), .b(adder_13_out), .out(sum[13]), .cin(adder_76_cout), .cout(adder_77_cout));
  Adder #(.width(1)) adder_78 (
    .a(adder_13_cout), .b(adder_14_out), .out(sum[14]), .cin(adder_77_cout), .cout(adder_78_cout));
  Adder #(.width(1)) adder_79 (
    .a(adder_14_cout), .b(adder_15_out), .out(sum[15]), .cin(adder_78_cout), .cout(adder_79_cout));
  Adder #(.width(1)) adder_80 (
    .a(adder_15_cout), .b(adder_16_out), .out(sum[16]), .cin(adder_79_cout), .cout(adder_80_cout));
  Adder #(.width(1)) adder_81 (
    .a(adder_16_cout), .b(adder_17_out), .out(sum[17]), .cin(adder_80_cout), .cout(adder_81_cout));
  Adder #(.width(1)) adder_82 (
    .a(adder_17_cout), .b(adder_18_out), .out(sum[18]), .cin(adder_81_cout), .cout(adder_82_cout));
  Adder #(.width(1)) adder_83 (
    .a(adder_18_cout), .b(adder_19_out), .out(sum[19]), .cin(adder_82_cout), .cout(adder_83_cout));
  Adder #(.width(1)) adder_84 (
    .a(adder_19_cout), .b(adder_20_out), .out(sum[20]), .cin(adder_83_cout), .cout(adder_84_cout));
  Adder #(.width(1)) adder_85 (
    .a(adder_20_cout), .b(adder_21_out), .out(sum[21]), .cin(adder_84_cout), .cout(adder_85_cout));
  Adder #(.width(1)) adder_86 (
    .a(adder_21_cout), .b(adder_22_out), .out(sum[22]), .cin(adder_85_cout), .cout(adder_86_cout));
  Adder #(.width(1)) adder_87 (
    .a(adder_22_cout), .b(adder_23_out), .out(sum[23]), .cin(adder_86_cout), .cout(adder_87_cout));
  Adder #(.width(1)) adder_88 (
    .a(adder_23_cout), .b(adder_24_out), .out(sum[24]), .cin(adder_87_cout), .cout(adder_88_cout));
  Adder #(.width(1)) adder_89 (
    .a(adder_24_cout), .b(adder_25_out), .out(sum[25]), .cin(adder_88_cout), .cout(adder_89_cout));
  Adder #(.width(1)) adder_90 (
    .a(adder_25_cout), .b(adder_26_out), .out(sum[26]), .cin(adder_89_cout), .cout(adder_90_cout));
  Adder #(.width(1)) adder_91 (
    .a(adder_26_cout), .b(adder_27_out), .out(sum[27]), .cin(adder_90_cout), .cout(adder_91_cout));
  Adder #(.width(1)) adder_92 (
    .a(adder_27_cout), .b(adder_28_out), .out(sum[28]), .cin(adder_91_cout), .cout(adder_92_cout));
  Adder #(.width(1)) adder_93 (
    .a(adder_28_cout), .b(adder_29_out), .out(sum[29]), .cin(adder_92_cout), .cout(adder_93_cout));
  Adder #(.width(1)) adder_94 (
    .a(adder_29_cout), .b(adder_30_out), .out(sum[30]), .cin(adder_93_cout), .cout(adder_94_cout));
  Adder #(.width(1)) adder_95 (
    .a(adder_30_cout), .b(adder_31_out), .out(sum[31]), .cin(adder_94_cout), .cout(adder_95_cout));
  Adder #(.width(1)) adder_96 (
    .a(adder_31_cout), .b(adder_32_out), .out(sum[32]), .cin(adder_95_cout), .cout(adder_96_cout));
  Adder #(.width(1)) adder_97 (
    .a(adder_32_cout), .b(adder_33_out), .out(sum[33]), .cin(adder_96_cout), .cout(adder_97_cout));
  Adder #(.width(1)) adder_98 (
    .a(adder_33_cout), .b(adder_34_out), .out(sum[34]), .cin(adder_97_cout), .cout(adder_98_cout));
  Adder #(.width(1)) adder_99 (
    .a(adder_34_cout), .b(adder_35_out), .out(sum[35]), .cin(adder_98_cout), .cout(adder_99_cout));
  Adder #(.width(1)) adder_100 (
    .a(adder_35_cout), .b(adder_36_out), .out(sum[36]), .cin(adder_99_cout), .cout(adder_100_cout));
  Adder #(.width(1)) adder_101 (
    .a(adder_36_cout), .b(adder_37_out), .out(sum[37]), .cin(adder_100_cout), .cout(adder_101_cout));
  Adder #(.width(1)) adder_102 (
    .a(adder_37_cout), .b(adder_38_out), .out(sum[38]), .cin(adder_101_cout), .cout(adder_102_cout));
  Adder #(.width(1)) adder_103 (
    .a(adder_38_cout), .b(adder_39_out), .out(sum[39]), .cin(adder_102_cout), .cout(adder_103_cout));
  Adder #(.width(1)) adder_104 (
    .a(adder_39_cout), .b(adder_40_out), .out(sum[40]), .cin(adder_103_cout), .cout(adder_104_cout));
  Adder #(.width(1)) adder_105 (
    .a(adder_40_cout), .b(adder_41_out), .out(sum[41]), .cin(adder_104_cout), .cout(adder_105_cout));
  Adder #(.width(1)) adder_106 (
    .a(adder_41_cout), .b(adder_42_out), .out(sum[42]), .cin(adder_105_cout), .cout(adder_106_cout));
  Adder #(.width(1)) adder_107 (
    .a(adder_42_cout), .b(adder_43_out), .out(sum[43]), .cin(adder_106_cout), .cout(adder_107_cout));
  Adder #(.width(1)) adder_108 (
    .a(adder_43_cout), .b(adder_44_out), .out(sum[44]), .cin(adder_107_cout), .cout(adder_108_cout));
  Adder #(.width(1)) adder_109 (
    .a(adder_44_cout), .b(adder_45_out), .out(sum[45]), .cin(adder_108_cout), .cout(adder_109_cout));
  Adder #(.width(1)) adder_110 (
    .a(adder_45_cout), .b(adder_46_out), .out(sum[46]), .cin(adder_109_cout), .cout(adder_110_cout));
  Adder #(.width(1)) adder_111 (
    .a(adder_46_cout), .b(adder_47_out), .out(sum[47]), .cin(adder_110_cout), .cout(adder_111_cout));
  Adder #(.width(1)) adder_112 (
    .a(adder_47_cout), .b(adder_48_out), .out(sum[48]), .cin(adder_111_cout), .cout(adder_112_cout));
  Adder #(.width(1)) adder_113 (
    .a(adder_48_cout), .b(adder_49_out), .out(sum[49]), .cin(adder_112_cout), .cout(adder_113_cout));
  Adder #(.width(1)) adder_114 (
    .a(adder_49_cout), .b(adder_50_out), .out(sum[50]), .cin(adder_113_cout), .cout(adder_114_cout));
  Adder #(.width(1)) adder_115 (
    .a(adder_50_cout), .b(adder_51_out), .out(sum[51]), .cin(adder_114_cout), .cout(adder_115_cout));
  Adder #(.width(1)) adder_116 (
    .a(adder_51_cout), .b(adder_52_out), .out(sum[52]), .cin(adder_115_cout), .cout(adder_116_cout));
  Adder #(.width(1)) adder_117 (
    .a(adder_52_cout), .b(adder_53_out), .out(sum[53]), .cin(adder_116_cout), .cout(adder_117_cout));
  Adder #(.width(1)) adder_118 (
    .a(adder_53_cout), .b(adder_54_out), .out(sum[54]), .cin(adder_117_cout), .cout(adder_118_cout));
  Adder #(.width(1)) adder_119 (
    .a(adder_54_cout), .b(adder_55_out), .out(sum[55]), .cin(adder_118_cout), .cout(adder_119_cout));
  Adder #(.width(1)) adder_120 (
    .a(adder_55_cout), .b(adder_56_out), .out(sum[56]), .cin(adder_119_cout), .cout(adder_120_cout));
  Adder #(.width(1)) adder_121 (
    .a(adder_56_cout), .b(adder_57_out), .out(sum[57]), .cin(adder_120_cout), .cout(adder_121_cout));
  Adder #(.width(1)) adder_122 (
    .a(adder_57_cout), .b(adder_58_out), .out(sum[58]), .cin(adder_121_cout), .cout(adder_122_cout));
  Adder #(.width(1)) adder_123 (
    .a(adder_58_cout), .b(adder_59_out), .out(sum[59]), .cin(adder_122_cout), .cout(adder_123_cout));
  Adder #(.width(1)) adder_124 (
    .a(adder_59_cout), .b(adder_60_out), .out(sum[60]), .cin(adder_123_cout), .cout(adder_124_cout));
  Adder #(.width(1)) adder_125 (
    .a(adder_60_cout), .b(adder_61_out), .out(sum[61]), .cin(adder_124_cout), .cout(adder_125_cout));
  Adder #(.width(1)) adder_126 (
    .a(adder_61_cout), .b(adder_62_out), .out(sum[62]), .cin(adder_125_cout), .cout(adder_126_cout));
  Adder #(.width(1)) adder_127 (
    .a(adder_62_cout), .b(adder_63_out), .out(sum[63]), .cin(adder_126_cout));  // open: cout
endmodule
